// Digital circuit full_adder.dig as structural Verilog
module full_adder (
  input  A,
  input  B,
  input  C__in,
  output S,
  output C__out
);

  wire and_1_out, and_2_out, xor_1_out;

  xor xor_1 (xor_1_out, A, B);
  xor xor_2 (S, xor_1_out, C__in);
  and and_1 (and_1_out, C__in, xor_1_out);
  and and_2 (and_2_out, B, A);
  or or_1 (C__out, and_1_out, and_2_out);
endmodule
